# Fritzing sketch PulseBox (saved by Fritzing 0.9.3b)
breadboards: 1

parts:
  R1 = Resistor [tolerance=±5% resistance=1k package=THT]
  C1 = Electrolytic Capacitor [capacitance=10µF voltage=50V package="100 mil [THT, electrolytic]"]
  Q1 = PNP-Transistor [package="TO92 [THT]"]
  U1 = Voltage Regulator - 5V [package="TO220 [THT]"]
  U2 = atmega328 [package=dip]
  XTAL1 = Crystal [frequency="16 Mhz" package=THT]
  LED1 = LED - 3mm [color="Red (633nm)" package="3 mm [THT]"]
  24V = Screw terminal - 2 pins [package=THT]
  C2 = Capacitor [package=cap-pth-small2]
  U3 = Sharp PC817 [package=THT]
  Encoder_Input_[+_-_A_B] = screw terminal, 4 pins
  R2 = Resistor [tolerance=±5% resistance=10k package=THT]
  R3 = Resistor [tolerance=±5% resistance=10k package=THT]
  R4 = Resistor [tolerance=±5% resistance=1k package=THT]
  R5 = Resistor [tolerance=±5% resistance=1k package=THT]
  R6 = Resistor [tolerance=±5% resistance=1k package=THT]
  R7 = Resistor [tolerance=±5% resistance=1k package=THT]
  U4 = Sharp PC817 [package=THT]
  C3 = Capacitor [package=cap-pth-small2]
  R8 = Resistor [tolerance=±5% resistance=10k package=THT]
  U5 = Sharp PC817 [package=THT]
  R9 = Resistor [tolerance=±5% resistance=1k package=THT]
  R10 = Resistor [tolerance=±5% resistance=1k package=THT]
  U6 = Sharp PC817 [package=THT]
  R11 = Resistor [tolerance=±5% resistance=10k package=THT]
  Encoder_Output_[+_-_A_B] = screw terminal, 4 pins
  R12 = Resistor [tolerance=±5% resistance=10k package=THT]
  Q2 = PNP-Transistor [package="TO92 [THT]"]
  R13 = Resistor [tolerance=±5% resistance=10k package=THT]
  LED2 = LED - 3mm [color="Red (633nm)" package="3 mm [THT]"]
  R14 = Resistor [tolerance=±5% resistance=10k package=THT]
  LED3 = LED - 3mm [color="Red (633nm)" package="3 mm [THT]"]

nets:
  N1: R1.Pin_0, LED1.cathode
  GND: R1.Pin_1, C1.-, U1.GND, U2.GND, 24V.pin1, C2.2, U3.Pin_2, U3.Pin_3, Encoder_Input_[+_-_A_B].pin3, U4.Pin_2, U4.Pin_3, C3.2, U5.Pin_2, U5.Pin_3, U6.Pin_2, U6.Pin_3, Encoder_Output_[+_-_A_B].pin2, R13.Pin_1, R14.Pin_1
  N2: C1.+, Q1.E, U1.input_voltage, 24V.pin2, Encoder_Input_[+_-_A_B].pin4, R2.Pin_0, R3.Pin_0, Encoder_Output_[+_-_A_B].pin1, Q2.E
  N3: Q1.B, R11.Pin_0
  N4: Q1.C, Encoder_Output_[+_-_A_B].pin3, LED2.anode
  N5: U1.output_voltage, U2.VCC, U2.AVCC, LED1.anode, R8.Pin_1
  N6: U2.RESET, R8.Pin_0
  N7: U2.D2, U3.Pin_4
  N8: U2.D3_(PWM), U4.Pin_4
  N9: U2.XLAT1, XTAL1.pin_0, C3.1
  N10: U2.XLAT2, XTAL1.pin_1, C2.1
  N11: U2.D5_(PWM), R9.Pin_1
  N12: U2.D8, R10.Pin_1
  N13: U3.Pin_1, R5.Pin_0
  N14: Encoder_Input_[+_-_A_B].pin1, R3.Pin_1, R7.Pin_1
  N15: Encoder_Input_[+_-_A_B].pin2, R2.Pin_1, R4.Pin_1
  N16: R4.Pin_0, R5.Pin_1
  N17: R6.Pin_0, U4.Pin_1
  N18: R6.Pin_1, R7.Pin_0
  N19: U5.Pin_1, R9.Pin_0
  N20: U5.Pin_4, R11.Pin_1
  N21: R10.Pin_0, U6.Pin_1
  N22: U6.Pin_4, R12.Pin_1
  N23: Encoder_Output_[+_-_A_B].pin4, Q2.C, LED3.anode
  N24: R12.Pin_0, Q2.B
  N25: R13.Pin_0, LED2.cathode
  N26: R14.Pin_0, LED3.cathode
