# Fritzing sketch 16-MCIM - Schematics (saved by Fritzing 0.8.7b)

parts:
  J1 = Screw terminal - 2 pins [package=THT]
  U1 = Voltage Regulator - 5V [package="TO220 [THT]"]
  C2 = Electrolytic Capacitor [capacitance=10µF voltage=50V package="100 mil [THT, electrolytic]"]
  C1 = Electrolytic Capacitor [capacitance=10µF voltage=50V package="100 mil [THT, electrolytic]"]
  R1 = Resistor [tolerance=±5% resistance=10k package=THT]
  LED1 = LED - 3mm [color="Red (633nm)" package="3 mm [THT]"]
  U2 = TLP621 [package=THT]
  R2 = Resistor [tolerance=±5% resistance=1k package=THT]
  J2 = Screw terminal - 2 pins [package=THT]
  U3 = Voltage Regulator - 5V [package="TO220 [THT]"]
  C4 = Electrolytic Capacitor [capacitance=10µF voltage=50V package="100 mil [THT, electrolytic]"]
  C3 = Electrolytic Capacitor [capacitance=10µF voltage=50V package="100 mil [THT, electrolytic]"]
  R3 = Resistor [tolerance=±5% resistance=10k package=THT]
  R4 = Resistor [tolerance=±5% resistance=1k package=THT]
  LED2 = LED - 3mm [color="Red (633nm)" package="3 mm [THT]"]
  U4 = TLP621 [package=THT]
  J3 = Screw terminal - 2 pins [package=THT]
  J4 = Screw terminal - 2 pins [package=THT]
  U7 = Voltage Regulator - 5V [package="TO220 [THT]"]
  U5 = Voltage Regulator - 5V [package="TO220 [THT]"]
  C7 = Electrolytic Capacitor [capacitance=10µF voltage=50V package="100 mil [THT, electrolytic]"]
  C6 = Electrolytic Capacitor [capacitance=10µF voltage=50V package="100 mil [THT, electrolytic]"]
  C5 = Electrolytic Capacitor [capacitance=10µF voltage=50V package="100 mil [THT, electrolytic]"]
  C8 = Electrolytic Capacitor [capacitance=10µF voltage=50V package="100 mil [THT, electrolytic]"]
  R5 = Resistor [tolerance=±5% resistance=10k package=THT]
  R6 = Resistor [tolerance=±5% resistance=1k package=THT]
  R8 = Resistor [tolerance=±5% resistance=1k package=THT]
  R7 = Resistor [tolerance=±5% resistance=10k package=THT]
  LED4 = LED - 3mm [color="Red (633nm)" package="3 mm [THT]"]
  LED3 = LED - 3mm [color="Red (633nm)" package="3 mm [THT]"]
  U8 = TLP621 [package=THT]
  U6 = TLP621 [package=THT]
  J6 = Screw terminal - 2 pins [package=THT]
  J5 = Screw terminal - 2 pins [package=THT]
  J7 = Screw terminal - 2 pins [package=THT]
  J8 = Screw terminal - 2 pins [package=THT]
  U9 = Voltage Regulator - 5V [package="TO220 [THT]"]
  U11 = Voltage Regulator - 5V [package="TO220 [THT]"]
  U15 = Voltage Regulator - 5V [package="TO220 [THT]"]
  U13 = Voltage Regulator - 5V [package="TO220 [THT]"]
  C12 = Electrolytic Capacitor [capacitance=10µF voltage=50V package="100 mil [THT, electrolytic]"]
  C10 = Electrolytic Capacitor [capacitance=10µF voltage=50V package="100 mil [THT, electrolytic]"]
  C9 = Electrolytic Capacitor [capacitance=10µF voltage=50V package="100 mil [THT, electrolytic]"]
  C11 = Electrolytic Capacitor [capacitance=10µF voltage=50V package="100 mil [THT, electrolytic]"]
  C13 = Electrolytic Capacitor [capacitance=10µF voltage=50V package="100 mil [THT, electrolytic]"]
  C16 = Electrolytic Capacitor [capacitance=10µF voltage=50V package="100 mil [THT, electrolytic]"]
  C14 = Electrolytic Capacitor [capacitance=10µF voltage=50V package="100 mil [THT, electrolytic]"]
  C15 = Electrolytic Capacitor [capacitance=10µF voltage=50V package="100 mil [THT, electrolytic]"]
  R14 = Resistor [tolerance=±5% resistance=1k package=THT]
  R12 = Resistor [tolerance=±5% resistance=1k package=THT]
  R16 = Resistor [tolerance=±5% resistance=1k package=THT]
  R13 = Resistor [tolerance=±5% resistance=10k package=THT]
  R11 = Resistor [tolerance=±5% resistance=10k package=THT]
  R9 = Resistor [tolerance=±5% resistance=10k package=THT]
  R15 = Resistor [tolerance=±5% resistance=10k package=THT]
  R10 = Resistor [tolerance=±5% resistance=1k package=THT]
  LED6 = LED - 3mm [color="Red (633nm)" package="3 mm [THT]"]
  LED8 = LED - 3mm [color="Red (633nm)" package="3 mm [THT]"]
  LED5 = LED - 3mm [color="Red (633nm)" package="3 mm [THT]"]
  LED7 = LED - 3mm [color="Red (633nm)" package="3 mm [THT]"]
  U16 = TLP621 [package=THT]
  U14 = TLP621 [package=THT]
  U10 = TLP621 [package=THT]
  U12 = TLP621 [package=THT]
  U17 = atmega328 [package=dip]
  XTAL1 = Crystal [frequency="16 Mhz" package=THT]
  C18 = Capacitor [package=cap-pth-small2]
  C19 = Capacitor [package=cap-pth-small2]
  S1 = Pushbutton [package="[THT]"]
  USB2TTL1 = screw terminal, 4 pins
  R17 = Resistor [tolerance=±5% resistance=1k package=THT]
  J11 = Screw terminal - 2 pins [package=THT]
  J12 = Screw terminal - 2 pins [package=THT]
  J15 = Screw terminal - 2 pins [package=THT]
  J9 = Screw terminal - 2 pins [package=THT]
  J13 = Screw terminal - 2 pins [package=THT]
  J10 = Screw terminal - 2 pins [package=THT]
  J14 = Screw terminal - 2 pins [package=THT]
  J16 = Screw terminal - 2 pins [package=THT]
  U31 = Voltage Regulator - 5V [package="TO220 [THT]"]
  U29 = Voltage Regulator - 5V [package="TO220 [THT]"]
  U25 = Voltage Regulator - 5V [package="TO220 [THT]"]
  U23 = Voltage Regulator - 5V [package="TO220 [THT]"]
  U21 = Voltage Regulator - 5V [package="TO220 [THT]"]
  U19 = Voltage Regulator - 5V [package="TO220 [THT]"]
  U17_2 = Voltage Regulator - 5V [package="TO220 [THT]"]
  U27 = Voltage Regulator - 5V [package="TO220 [THT]"]
  C17 = Electrolytic Capacitor [capacitance=10µF voltage=50V package="100 mil [THT, electrolytic]"]
  C20 = Electrolytic Capacitor [capacitance=10µF voltage=50V package="100 mil [THT, electrolytic]"]
  C29 = Electrolytic Capacitor [capacitance=10µF voltage=50V package="100 mil [THT, electrolytic]"]
  C22 = Electrolytic Capacitor [capacitance=10µF voltage=50V package="100 mil [THT, electrolytic]"]
  C28 = Electrolytic Capacitor [capacitance=10µF voltage=50V package="100 mil [THT, electrolytic]"]
  C30 = Electrolytic Capacitor [capacitance=10µF voltage=50V package="100 mil [THT, electrolytic]"]
  C31 = Electrolytic Capacitor [capacitance=10µF voltage=50V package="100 mil [THT, electrolytic]"]
  C21 = Electrolytic Capacitor [capacitance=10µF voltage=50V package="100 mil [THT, electrolytic]"]
  C32 = Electrolytic Capacitor [capacitance=10µF voltage=50V package="100 mil [THT, electrolytic]"]
  C18_2 = Electrolytic Capacitor [capacitance=10µF voltage=50V package="100 mil [THT, electrolytic]"]
  C19_2 = Electrolytic Capacitor [capacitance=10µF voltage=50V package="100 mil [THT, electrolytic]"]
  C23 = Electrolytic Capacitor [capacitance=10µF voltage=50V package="100 mil [THT, electrolytic]"]
  C25 = Electrolytic Capacitor [capacitance=10µF voltage=50V package="100 mil [THT, electrolytic]"]
  C27 = Electrolytic Capacitor [capacitance=10µF voltage=50V package="100 mil [THT, electrolytic]"]
  C26 = Electrolytic Capacitor [capacitance=10µF voltage=50V package="100 mil [THT, electrolytic]"]
  C24 = Electrolytic Capacitor [capacitance=10µF voltage=50V package="100 mil [THT, electrolytic]"]
  R19 = Resistor [tolerance=±5% resistance=10k package=THT]
  R29 = Resistor [tolerance=±5% resistance=10k package=THT]
  R24 = Resistor [tolerance=±5% resistance=1k package=THT]
  R26 = Resistor [tolerance=±5% resistance=1k package=THT]
  R20 = Resistor [tolerance=±5% resistance=1k package=THT]
  R25 = Resistor [tolerance=±5% resistance=10k package=THT]
  R28 = Resistor [tolerance=±5% resistance=1k package=THT]
  R31 = Resistor [tolerance=±5% resistance=10k package=THT]
  R32 = Resistor [tolerance=±5% resistance=1k package=THT]
  R30 = Resistor [tolerance=±5% resistance=1k package=THT]
  R21 = Resistor [tolerance=±5% resistance=10k package=THT]
  R18 = Resistor [tolerance=±5% resistance=1k package=THT]
  R17_2 = Resistor [tolerance=±5% resistance=10k package=THT]
  R23 = Resistor [tolerance=±5% resistance=10k package=THT]
  R22 = Resistor [tolerance=±5% resistance=1k package=THT]
  R27 = Resistor [tolerance=±5% resistance=10k package=THT]
  LED15 = LED - 3mm [color="Red (633nm)" package="3 mm [THT]"]
  LED14 = LED - 3mm [color="Red (633nm)" package="3 mm [THT]"]
  LED13 = LED - 3mm [color="Red (633nm)" package="3 mm [THT]"]
  LED16 = LED - 3mm [color="Red (633nm)" package="3 mm [THT]"]
  LED12 = LED - 3mm [color="Red (633nm)" package="3 mm [THT]"]
  LED11 = LED - 3mm [color="Red (633nm)" package="3 mm [THT]"]
  LED9 = LED - 3mm [color="Red (633nm)" package="3 mm [THT]"]
  LED10 = LED - 3mm [color="Red (633nm)" package="3 mm [THT]"]
  U22 = TLP621 [package=THT]
  U32 = TLP621 [package=THT]
  U20 = TLP621 [package=THT]
  U28 = TLP621 [package=THT]
  U24 = TLP621 [package=THT]
  U30 = TLP621 [package=THT]
  U26 = TLP621 [package=THT]
  U18 = TLP621 [package=THT]

nets:
  N1: J1.pin1, U1.input_voltage, C1.+
  N2: J1.pin2, U1.GND, C2.-, C1.-, LED1.cathode, U2.Pin_2
  N3: U1.output_voltage, C2.+, R1.Pin_0, R2.Pin_0
  N4: R1.Pin_1, LED1.anode
  N5: U2.Pin_1, R2.Pin_1
  N6: U2.Pin_4, U17.D2
  GND: U2.Pin_3, U4.Pin_3, U8.Pin_3, U6.Pin_3, U16.Pin_3, U14.Pin_3, U10.Pin_3, U12.Pin_3, U17.GND, C18.2, C19.2, S1.Pin_3, S1.Pin_4, USB2TTL1.pin3, U22.Pin_3, U32.Pin_3, U20.Pin_3, U28.Pin_3, U24.Pin_3, U30.Pin_3, U26.Pin_3, U18.Pin_3
  N7: J2.pin1, U3.input_voltage, C3.+
  N8: J2.pin2, U3.GND, C4.-, C3.-, LED2.cathode, U4.Pin_2
  N9: U3.output_voltage, C4.+, R3.Pin_0, R4.Pin_0
  N10: R3.Pin_1, LED2.anode
  N11: R4.Pin_1, U4.Pin_1
  N12: U4.Pin_4, U17.D3_(PWM)
  N13: J3.pin1, U5.input_voltage, C5.+
  N14: J3.pin2, U5.GND, C6.-, C5.-, LED3.cathode, U6.Pin_2
  N15: J4.pin1, U7.input_voltage, C7.+
  N16: J4.pin2, U7.GND, C7.-, C8.-, LED4.cathode, U8.Pin_2
  N17: U7.output_voltage, C8.+, R8.Pin_0, R7.Pin_0
  N18: U5.output_voltage, C6.+, R5.Pin_0, R6.Pin_0
  N19: R5.Pin_1, LED3.anode
  N20: R6.Pin_1, U6.Pin_1
  N21: R8.Pin_1, U8.Pin_1
  N22: R7.Pin_1, LED4.anode
  N23: U8.Pin_4, U17.D5_(PWM)
  N24: U6.Pin_4, U17.D4
  N25: J6.pin1, U11.input_voltage, C11.+
  N26: J6.pin2, U11.GND, C12.-, C11.-, LED6.cathode, U12.Pin_2
  N27: J5.pin1, U9.input_voltage, C9.+
  N28: J5.pin2, U9.GND, C10.-, C9.-, LED5.cathode, U10.Pin_2
  N29: J7.pin1, U13.input_voltage, C13.+
  N30: J7.pin2, U13.GND, C13.-, C14.-, LED7.cathode, U14.Pin_2
  N31: J8.pin1, U15.input_voltage, C15.+
  N32: J8.pin2, U15.GND, C16.-, C15.-, LED8.cathode, U16.Pin_2
  N33: U9.output_voltage, C10.+, R9.Pin_0, R10.Pin_0
  N34: U11.output_voltage, C12.+, R12.Pin_0, R11.Pin_0
  N35: U15.output_voltage, C16.+, R16.Pin_0, R15.Pin_0
  N36: U13.output_voltage, C14.+, R14.Pin_0, R13.Pin_0
  N37: R14.Pin_1, U14.Pin_1
  N38: R12.Pin_1, U12.Pin_1
  N39: R16.Pin_1, U16.Pin_1
  N40: R13.Pin_1, LED7.anode
  N41: R11.Pin_1, LED6.anode
  N42: R9.Pin_1, LED5.anode
  N43: R15.Pin_1, LED8.anode
  N44: R10.Pin_1, U10.Pin_1
  N45: U16.Pin_4, U17.D9_(PWM)
  N46: U14.Pin_4, U17.D8
  N47: U10.Pin_4, U17.D6_(PWM)
  N48: U12.Pin_4, U17.D7
  N49: U17.RESET, S1.Pin_1, S1.Pin_2, R17.Pin_0
  N50: U17.D0_(RX), USB2TTL1.pin1
  N51: U17.D1_(TX), USB2TTL1.pin2
  N52: U17.VCC, U17.AVCC, USB2TTL1.pin4, R17.Pin_1
  N53: U17.XLAT1, XTAL1.pin_0, C18.1
  N54: U17.XLAT2, XTAL1.pin_1, C19.1
  N55: U17.D10_(PWM), U18.Pin_4
  N56: U17.D11_(PWM), U20.Pin_4
  N57: U17.D12, U22.Pin_4
  N58: U17.D13, U24.Pin_4
  N59: U17.A0, U26.Pin_4
  N60: U17.A1, U28.Pin_4
  N61: U17.A2, U30.Pin_4
  N62: U17.A3, U32.Pin_4
  N63: J11.pin1, U21.input_voltage, C21.+
  N64: J11.pin2, U21.GND, C22.-, C21.-, LED11.cathode, U22.Pin_2
  N65: J12.pin1, U23.input_voltage, C23.+
  N66: J12.pin2, U23.GND, C23.-, C24.-, LED12.cathode, U24.Pin_2
  N67: J15.pin1, U29.input_voltage, C29.+
  N68: J15.pin2, U29.GND, C29.-, C30.-, LED15.cathode, U30.Pin_2
  N69: J9.pin1, U17_2.input_voltage, C17.+
  N70: J9.pin2, U17_2.GND, C17.-, C18_2.-, LED9.cathode, U18.Pin_2
  N71: J13.pin1, U25.input_voltage, C25.+
  N72: J13.pin2, U25.GND, C25.-, C26.-, LED13.cathode, U26.Pin_2
  N73: J10.pin1, U19.input_voltage, C19_2.+
  N74: J10.pin2, U19.GND, C20.-, C19_2.-, LED10.cathode, U20.Pin_2
  N75: J14.pin1, U27.input_voltage, C27.+
  N76: J14.pin2, U27.GND, C28.-, C27.-, LED14.cathode, U28.Pin_2
  N77: J16.pin1, U31.input_voltage, C31.+
  N78: J16.pin2, U31.GND, C31.-, C32.-, LED16.cathode, U32.Pin_2
  N79: U31.output_voltage, C32.+, R31.Pin_0, R32.Pin_0
  N80: U29.output_voltage, C30.+, R29.Pin_0, R30.Pin_0
  N81: U25.output_voltage, C26.+, R26.Pin_0, R25.Pin_0
  N82: U23.output_voltage, C24.+, R24.Pin_0, R23.Pin_0
  N83: U21.output_voltage, C22.+, R21.Pin_0, R22.Pin_0
  N84: U19.output_voltage, C20.+, R19.Pin_0, R20.Pin_0
  N85: U17_2.output_voltage, C18_2.+, R18.Pin_0, R17_2.Pin_0
  N86: U27.output_voltage, C28.+, R28.Pin_0, R27.Pin_0
  N87: R19.Pin_1, LED10.anode
  N88: R29.Pin_1, LED15.anode
  N89: R24.Pin_1, U24.Pin_1
  N90: R26.Pin_1, U26.Pin_1
  N91: R20.Pin_1, U20.Pin_1
  N92: R25.Pin_1, LED13.anode
  N93: R28.Pin_1, U28.Pin_1
  N94: R31.Pin_1, LED16.anode
  N95: R32.Pin_1, U32.Pin_1
  N96: R30.Pin_1, U30.Pin_1
  N97: R21.Pin_1, LED11.anode
  N98: R18.Pin_1, U18.Pin_1
  N99: R17_2.Pin_1, LED9.anode
  N100: R23.Pin_1, LED12.anode
  N101: R22.Pin_1, U22.Pin_1
  N102: R27.Pin_1, LED14.anode
