# Fritzing sketch 16-MCIM (saved by Fritzing 0.8.7b)
circuit board: 9.65cm x 17cm
breadboards: 1

parts:
  VR1 = Voltage Regulator [package=to220-igo]
  C1 = Capacitor Polarized [package=cpol-radial-10uf-25v]
  R1 = Resistor [tolerance=±5% resistance=1k package=THT]
  R2 = Resistor [tolerance=±5% resistance=10k package=THT]
  U1 = TLP621 [package=THT]
  LED1 = LTE-302 [package=lte-302]
  J1 = Screw terminal - 2 pins [package=THT]
  C2 = Capacitor Polarized [package=cpol-radial-10uf-25v]
  VR2 = Voltage Regulator [package=to220-igo]
  C3 = Capacitor Polarized [package=cpol-radial-10uf-25v]
  C4 = Capacitor Polarized [package=cpol-radial-10uf-25v]
  R3 = Resistor [tolerance=±5% resistance=10k package=THT]
  R4 = Resistor [tolerance=±5% resistance=1k package=THT]
  U2 = TLP621 [package=THT]
  LED2 = LTE-302 [package=lte-302]
  J2 = Screw terminal - 2 pins [package=THT]
  VR3 = Voltage Regulator [package=to220-igo]
  C5 = Capacitor Polarized [package=cpol-radial-10uf-25v]
  C6 = Capacitor Polarized [package=cpol-radial-10uf-25v]
  R5 = Resistor [tolerance=±5% resistance=10k package=THT]
  R6 = Resistor [tolerance=±5% resistance=1k package=THT]
  U3 = TLP621 [package=THT]
  LED3 = LTE-302 [package=lte-302]
  J3 = Screw terminal - 2 pins [package=THT]
  VR4 = Voltage Regulator [package=to220-igo]
  C7 = Capacitor Polarized [package=cpol-radial-10uf-25v]
  C8 = Capacitor Polarized [package=cpol-radial-10uf-25v]
  R7 = Resistor [tolerance=±5% resistance=10k package=THT]
  R8 = Resistor [tolerance=±5% resistance=1k package=THT]
  U4 = TLP621 [package=THT]
  LED4 = LTE-302 [package=lte-302]
  J4 = Screw terminal - 2 pins [package=THT]
  VR5 = Voltage Regulator [package=to220-igo]
  VR6 = Voltage Regulator [package=to220-igo]
  VR7 = Voltage Regulator [package=to220-igo]
  VR8 = Voltage Regulator [package=to220-igo]
  C9 = Capacitor Polarized [package=cpol-radial-10uf-25v]
  C10 = Capacitor Polarized [package=cpol-radial-10uf-25v]
  C11 = Capacitor Polarized [package=cpol-radial-10uf-25v]
  C12 = Capacitor Polarized [package=cpol-radial-10uf-25v]
  C13 = Capacitor Polarized [package=cpol-radial-10uf-25v]
  C14 = Capacitor Polarized [package=cpol-radial-10uf-25v]
  C15 = Capacitor Polarized [package=cpol-radial-10uf-25v]
  C16 = Capacitor Polarized [package=cpol-radial-10uf-25v]
  R9 = Resistor [tolerance=±5% resistance=10k package=THT]
  R10 = Resistor [tolerance=±5% resistance=10k package=THT]
  R11 = Resistor [tolerance=±5% resistance=10k package=THT]
  R12 = Resistor [tolerance=±5% resistance=10k package=THT]
  R13 = Resistor [tolerance=±5% resistance=1k package=THT]
  R14 = Resistor [tolerance=±5% resistance=1k package=THT]
  R15 = Resistor [tolerance=±5% resistance=1k package=THT]
  R16 = Resistor [tolerance=±5% resistance=1k package=THT]
  U5 = TLP621 [package=THT]
  U6 = TLP621 [package=THT]
  U7 = TLP621 [package=THT]
  U8 = TLP621 [package=THT]
  LED5 = LTE-302 [package=lte-302]
  LED6 = LTE-302 [package=lte-302]
  LED7 = LTE-302 [package=lte-302]
  LED8 = LTE-302 [package=lte-302]
  J5 = Screw terminal - 2 pins [package=THT]
  J6 = Screw terminal - 2 pins [package=THT]
  J7 = Screw terminal - 2 pins [package=THT]
  J8 = Screw terminal - 2 pins [package=THT]
  VR9 = Voltage Regulator [package=to220-igo]
  VR10 = Voltage Regulator [package=to220-igo]
  C17 = Capacitor Polarized [package=cpol-radial-10uf-25v]
  C18 = Capacitor Polarized [package=cpol-radial-10uf-25v]
  C19 = Capacitor Polarized [package=cpol-radial-10uf-25v]
  C20 = Capacitor Polarized [package=cpol-radial-10uf-25v]
  R17 = Resistor [tolerance=±5% resistance=10k package=THT]
  R18 = Resistor [tolerance=±5% resistance=10k package=THT]
  R19 = Resistor [tolerance=±5% resistance=1k package=THT]
  R20 = Resistor [tolerance=±5% resistance=1k package=THT]
  U9 = TLP621 [package=THT]
  U10 = TLP621 [package=THT]
  LED9 = LTE-302 [package=lte-302]
  LED10 = LTE-302 [package=lte-302]
  J9 = Screw terminal - 2 pins [package=THT]
  J10 = Screw terminal - 2 pins [package=THT]
  VR11 = Voltage Regulator [package=to220-igo]
  VR12 = Voltage Regulator [package=to220-igo]
  VR13 = Voltage Regulator [package=to220-igo]
  VR15 = Voltage Regulator [package=to220-igo]
  VR16 = Voltage Regulator [package=to220-igo]
  C21 = Capacitor Polarized [package=cpol-radial-10uf-25v]
  C22 = Capacitor Polarized [package=cpol-radial-10uf-25v]
  C23 = Capacitor Polarized [package=cpol-radial-10uf-25v]
  C24 = Capacitor Polarized [package=cpol-radial-10uf-25v]
  C25 = Capacitor Polarized [package=cpol-radial-10uf-25v]
  C26 = Capacitor Polarized [package=cpol-radial-10uf-25v]
  C27 = Capacitor Polarized [package=cpol-radial-10uf-25v]
  C28 = Capacitor Polarized [package=cpol-radial-10uf-25v]
  C29 = Capacitor Polarized [package=cpol-radial-10uf-25v]
  C30 = Capacitor Polarized [package=cpol-radial-10uf-25v]
  C31 = Capacitor Polarized [package=cpol-radial-10uf-25v]
  C32 = Capacitor Polarized [package=cpol-radial-10uf-25v]
  R23 = Resistor [tolerance=±5% resistance=10k package=THT]
  R24 = Resistor [tolerance=±5% resistance=10k package=THT]
  R25 = Resistor [tolerance=±5% resistance=10k package=THT]
  R26 = Resistor [tolerance=±5% resistance=10k package=THT]
  R27 = Resistor [tolerance=±5% resistance=10k package=THT]
  R28 = Resistor [tolerance=±5% resistance=10k package=THT]
  R29 = Resistor [tolerance=±5% resistance=1k package=THT]
  R30 = Resistor [tolerance=±5% resistance=1k package=THT]
  R31 = Resistor [tolerance=±5% resistance=1k package=THT]
  R32 = Resistor [tolerance=±5% resistance=1k package=THT]
  R33 = Resistor [tolerance=±5% resistance=1k package=THT]
  R34 = Resistor [tolerance=±5% resistance=1k package=THT]
  U11 = TLP621 [package=THT]
  U12 = TLP621 [package=THT]
  U13 = TLP621 [package=THT]
  U14 = TLP621 [package=THT]
  U15 = TLP621 [package=THT]
  U16 = TLP621 [package=THT]
  LED11 = LTE-302 [package=lte-302]
  LED12 = LTE-302 [package=lte-302]
  LED13 = LTE-302 [package=lte-302]
  LED14 = LTE-302 [package=lte-302]
  LED15 = LTE-302 [package=lte-302]
  LED16 = LTE-302 [package=lte-302]
  J11 = Screw terminal - 2 pins [package=THT]
  J12 = Screw terminal - 2 pins [package=THT]
  J13 = Screw terminal - 2 pins [package=THT]
  J14 = Screw terminal - 2 pins [package=THT]
  J15 = Screw terminal - 2 pins [package=THT]
  J16 = Screw terminal - 2 pins [package=THT]
  U18 = atmega328 [package=dip]
  XTAL1 = Crystal [frequency="16 Mhz" package=THT]
  C33 = Capacitor [package=cap-pth-small-kit]
  C34 = Capacitor [package=cap-pth-small-kit]
  R35 = Resistor [tolerance=±5% resistance=10k package=THT]
  S1 = Pushbutton [package="[THT]"]
  USB2TTL = screw terminal, 4 pins
  VR14 = Voltage Regulator [package=to220-igo]

nets:
  N1: VR1.IN, C1.+, J1.pin2
  N2: VR1.OUT, R1.Pin_0, R2.Pin_0, C2.+
  N3: R1.Pin_1, U1.Pin_1
  N4: R2.Pin_1, LED1.A
  N5: U1.Pin_4, U18.D8
  N6: VR2.IN, C4.+, J2.pin2
  N7: VR2.OUT, C3.+, R3.Pin_0, R4.Pin_0
  N8: R3.Pin_1, LED2.A
  N9: R4.Pin_1, U2.Pin_1
  N10: U2.Pin_4, U18.D7
  N11: VR3.IN, C6.+, J3.pin2
  N12: VR3.OUT, C5.+, R5.Pin_0, R6.Pin_0
  N13: R5.Pin_1, LED3.A
  N14: R6.Pin_1, U3.Pin_1
  N15: U3.Pin_4, U18.D6_(PWM)
  N16: VR4.IN, C8.+, J4.pin2
  N17: VR4.OUT, C7.+, R7.Pin_0, R8.Pin_0
  N18: R7.Pin_1, LED4.A
  N19: R8.Pin_1, U4.Pin_1
  N20: U4.Pin_4, U18.D5_(PWM)
  N21: VR5.IN, C11.+, J7.pin2
  N22: VR5.OUT, C14.+, R10.Pin_0, R15.Pin_0
  N23: VR6.IN, C15.+, J8.pin2
  N24: VR6.OUT, C13.+, R12.Pin_0, R14.Pin_0
  N25: VR7.IN, C10.+, J6.pin2
  N26: VR7.OUT, C12.+, R11.Pin_0, R13.Pin_0
  N27: VR8.IN, C16.+, J5.pin2
  N28: VR8.OUT, C9.+, R9.Pin_0, R16.Pin_0
  N29: R9.Pin_1, LED8.A
  N30: R10.Pin_1, LED5.A
  N31: R11.Pin_1, LED7.A
  N32: R12.Pin_1, LED6.A
  N33: R13.Pin_1, U6.Pin_1
  N34: R14.Pin_1, U7.Pin_1
  N35: R15.Pin_1, U5.Pin_1
  N36: R16.Pin_1, U8.Pin_1
  N37: U5.Pin_4, U18.A5
  N38: U6.Pin_4, U18.D2
  N39: U7.Pin_4, U18.D3_(PWM)
  N40: U8.Pin_4, U18.D4
  N41: VR9.IN, C18.+, J9.pin2
  N42: VR9.OUT, C17.+, R18.Pin_0, R19.Pin_0
  N43: VR10.IN, C19.+, J10.pin2
  N44: VR10.OUT, C20.+, R17.Pin_0, R20.Pin_0
  N45: R17.Pin_1, LED9.A
  N46: R18.Pin_1, LED10.A
  N47: R19.Pin_1, U10.Pin_1
  N48: R20.Pin_1, U9.Pin_1
  N49: U9.Pin_4, U18.A3
  N50: U10.Pin_4, U18.A4
  N51: VR11.IN, C30.+, J16.pin2
  N52: VR11.OUT, C25.+, R24.Pin_0, R32.Pin_0
  N53: VR12.IN, C27.+, J14.pin2
  N54: VR12.OUT, C26.+, R23.Pin_0, R34.Pin_0
  N55: VR13.IN, C31.+, J15.pin2
  N56: VR13.OUT, C21.+, R28.Pin_0, R29.Pin_0
  N57: VR15.IN, C24.+, J11.pin2
  N58: VR15.OUT, C29.+, R26.Pin_0, R31.Pin_0
  N59: VR16.IN, C23.+, J13.pin2
  N60: VR16.OUT, C22.+, R25.Pin_0, R33.Pin_0
  N61: C28.+, J12.pin2, VR14.IN
  N62: C32.+, R27.Pin_0, R30.Pin_0, VR14.OUT
  N63: R23.Pin_1, LED11.A
  N64: R24.Pin_1, LED14.A
  N65: R25.Pin_1, LED15.A
  N66: R26.Pin_1, LED13.A
  N67: R27.Pin_1, LED12.A
  N68: R28.Pin_1, LED16.A
  N69: R29.Pin_1, U14.Pin_1
  N70: R30.Pin_1, U12.Pin_1
  N71: R31.Pin_1, U15.Pin_1
  N72: R32.Pin_1, U11.Pin_1
  N73: R33.Pin_1, U16.Pin_1
  N74: R34.Pin_1, U13.Pin_1
  N75: U11.Pin_4, U18.A2
  N76: U12.Pin_4, U18.D9_(PWM)
  N77: U13.Pin_4, U18.D11_(PWM)
  N78: U14.Pin_4, U18.D10_(PWM)
  N79: U15.Pin_4, U18.A1
  N80: U16.Pin_4, U18.A0
  N81: U18.RESET, R35.Pin_0, S1.Pin_1, S1.Pin_2
  N82: U18.D0_(RX), USB2TTL.pin4
  N83: U18.D1_(TX), USB2TTL.pin3
  N84: U18.VCC, U18.AVCC, R35.Pin_1, USB2TTL.pin1
  N85: U18.XLAT1, XTAL1.pin_1, C33.1
  N86: U18.XLAT2, XTAL1.pin_0, C34.1
  N87: S1.Pin_3, S1.Pin_4
