# Fritzing sketch Level Shifter and Switcher - 5-40V Input - 5V Sensor Output - 5-40V Output - Positive Output (saved by Fritzing 0.8.7b)
stripboards: 1

parts:
  R1 = Resistor [tolerance=±5% resistance=10k package=THT]
  U1 = Voltage Regulator - 5V [package="TO220 [THT]"]
  Sensor_Pinouts = Header 3 [package=molex-1x3_lock]
  Power_Supply_(24V) = Header 2 [package=molex-1x2_lock]
  C1 = Electrolytic Capacitor [capacitance=10µF voltage=25V package="200 mil [THT, electrolytic]"]
  Q1 = PNP-Transistor [package="TO92 [THT]"]
  Output = Header 2 [package=molex-1x2_lock]
  R4 = Resistor [tolerance=±5% resistance=10k package=THT]
  R5 = Resistor [tolerance=±5% resistance=1k package=THT]
  Q2 = NPN-Transistor [package="TO92 [THT]"]  # not connected
  U2 = TLP621 [package=THT]
  LED1 = LED - 3mm [color="Red (633nm)" package="3 mm [THT]"]

nets:
  N1: R1.Pin_0, U2.Pin_4
  N2: R1.Pin_1, Q1.B
  N3: U1.input_voltage, Power_Supply_(24V).1, C1.+, Q1.E
  N4: U1.GND, Sensor_Pinouts.2, Power_Supply_(24V).2, C1.-, Output.2, U2.Pin_2, U2.Pin_3, LED1.cathode
  N5: U1.output_voltage, Sensor_Pinouts.1
  N6: Sensor_Pinouts.3, R5.Pin_0
  N7: Q1.C, Output.1
  N8: R4.Pin_1, LED1.anode
  N9: R5.Pin_1, U2.Pin_1
