# Fritzing sketch Light Activated Switch (saved by Fritzing 0.8.7b)
breadboards: 1

parts:
  U1 = Voltage Regulator - 5V [package="TO220 [THT]"]
  Output = Header 2 [package=molex-1x2_lock]
  Power_Supply_(24V) = Header 2 [package=molex-1x2_lock]
  C2 = Electrolytic Capacitor [capacitance=10µF voltage=25V package="200 mil [THT, electrolytic]"]
  R3 = Resistor [tolerance=±5% resistance=1k package=THT]
  R1 = Resistor [tolerance=±5% resistance=1k package=THT]
  Q1 = NPN-Transistor [package="TO92 [THT]"]
  Q2 = PNP-Transistor [package="TO92 [THT]"]
  R5 = Resistor [tolerance=±5% resistance=10k package=THT]
  R7 = Photocell (LDR) [package=THT]
  LED2 = LED - 3mm [color="Red (633nm)" package="3 mm [THT]"]
  Input = Header 4 [package=molex-1x4_lock]
  R8 = Resistor [tolerance=±5% resistance=1k package=THT]

nets:
  N1: U1.input_voltage, Power_Supply_(24V).1, C2.+, Q2.E
  N2: U1.output_voltage, R7.pin_1, Input.3
  N3: Output.1, Q2.C
  N4: Output.2, Power_Supply_(24V).2, C2.-, R1.Pin_1, Q1.E
  N5: R3.Pin_1, Q1.B
  N6: R1.Pin_0, R7.pin_0, Input.4
  N7: Q1.C, R5.Pin_1, R8.Pin_0
  N8: Q2.B, R5.Pin_0
  N9: LED2.cathode, Input.2
  N10: LED2.anode, Input.1, R8.Pin_1
