# Fritzing sketch Signal Isolator (24V) - Positive Output (saved by Fritzing 0.8.7b)
breadboards: 1

parts:
  R1 = Resistor [tolerance=±5% resistance=1k package=THT]
  Q1 = NPN-Transistor [package="TO92 [THT]"]
  U1 = Voltage Regulator - 5V [package="TO220 [THT]"]
  U2 = TLP621 [package=THT]
  Sensor_Pinouts = Header 3 [package=molex-1x3_lock]
  Sensor_Power_Supply_(24V) = Header 2 [package=molex-1x2_lock]
  C1 = Electrolytic Capacitor [capacitance=10µF voltage=25V package="200 mil [THT, electrolytic]"]
  Independent_Power_Supply_(24V) = Header 2 [package=molex-1x2_lock]
  U3 = Voltage Regulator - 5V [package="TO220 [THT]"]
  C2 = Electrolytic Capacitor [capacitance=10µF voltage=25V package="200 mil [THT, electrolytic]"]
  R2 = Resistor [tolerance=±5% resistance=1k package=THT]
  R3 = Resistor [tolerance=±5% resistance=10k package=THT]
  Output = Header 2 [package=molex-1x2_lock]
  LED = LED - 3mm [color="Red (633nm)" package="3 mm [THT]"]
  R4 = Resistor [tolerance=±5% resistance=1k package=THT]
  Q2 = PNP-Transistor [package="TO92 [THT]"]

nets:
  N1: R1.Pin_0, U1.output_voltage
  N2: R1.Pin_1, U2.Pin_1
  N3: Q1.E, Independent_Power_Supply_(24V).2, U3.GND, C2.-, Output.2
  N4: Q1.B, R2.Pin_1
  N5: Q1.C, LED.cathode, R4.Pin_0
  N6: U1.input_voltage, Sensor_Pinouts.3, C1.+
  N7: U1.GND, U2.Pin_2, Sensor_Pinouts.2, C1.-
  N8: U2.Pin_4, U3.output_voltage, R3.Pin_0
  N9: U2.Pin_3, R2.Pin_0
  N10: Sensor_Pinouts.1, Sensor_Power_Supply_(24V).1
  N11: Independent_Power_Supply_(24V).1, U3.input_voltage, C2.+, Q2.E
  N12: R3.Pin_1, LED.anode
  N13: Output.1, Q2.C
  N14: R4.Pin_1, Q2.B
