# Fritzing sketch Signal Isolator - Positive Output - V2 Lite (saved by Fritzing 0.8.7b)
breadboards: 1

parts:
  Q1 = PNP-Transistor [package="TO92 [THT]"]
  R4 = Resistor [tolerance=±5% resistance=10k package=THT]
  R2 = Resistor [tolerance=±5% resistance=1k package=THT]
  U1 = TLP621 [package=THT]
  Output = Header 2 [package=molex-1x2_lock]
  Independent_Power_Supply_(24V) = Header 2 [package=molex-1x2_lock]
  Sensor_Power_Supply_(24V) = Header 2 [package=molex-1x2_lock]
  Sensor_Pinouts = Header 3 [package=molex-1x3_lock]
  R3 = Resistor [tolerance=±5% resistance=10k package=THT]
  LED1 = LED - 3mm [color="Red (633nm)" package="3 mm [THT]"]
  R1 = Resistor [tolerance=±5% resistance=1k package=THT]

nets:
  N1: Q1.E, Independent_Power_Supply_(24V).2
  N2: Q1.B, R3.Pin_0
  N3: Q1.C, Output.2, LED1.anode
  N4: R4.Pin_0, LED1.cathode
  N5: R4.Pin_1, U1.Pin_3, Output.1, Independent_Power_Supply_(24V).1
  N6: R2.Pin_0, R1.Pin_1
  N7: R2.Pin_1, U1.Pin_1
  N8: U1.Pin_2, Sensor_Power_Supply_(24V).2, Sensor_Pinouts.2
  N9: U1.Pin_4, R3.Pin_1
  N10: Sensor_Power_Supply_(24V).1, Sensor_Pinouts.1
  N11: Sensor_Pinouts.3, R1.Pin_0
