# Fritzing sketch Signal Isolator - Positive Output - V2 (saved by Fritzing 0.8.7b)
breadboards: 1

parts:
  Q1 = PNP-Transistor [package="TO92 [THT]"]
  R3 = Resistor [tolerance=±5% resistance=10k package=THT]
  R1 = Resistor [tolerance=±5% resistance=1k package=THT]
  U1 = Voltage Regulator - 5V [package="TO220 [THT]"]
  U2 = TLP621 [package=THT]
  Output = Header 2 [package=molex-1x2_lock]
  Independent_Power_Supply_(24V) = Header 2 [package=molex-1x2_lock]
  Sensor_Power_Supply_(24V) = Header 2 [package=molex-1x2_lock]
  Sensor_Pinouts = Header 3 [package=molex-1x3_lock]
  C1 = Electrolytic Capacitor [capacitance=10µF voltage=25V package="200 mil [THT, electrolytic]"]
  R2 = Resistor [tolerance=±5% resistance=10k package=THT]
  LED1 = LED - 3mm [color="Red (633nm)" package="3 mm [THT]"]

nets:
  N1: Q1.E, Independent_Power_Supply_(24V).2
  N2: Q1.B, R2.Pin_0
  N3: Q1.C, Output.2, LED1.anode
  N4: R3.Pin_0, LED1.cathode
  N5: R3.Pin_1, U1.GND, U2.Pin_2, Sensor_Power_Supply_(24V).2, Sensor_Pinouts.2, C1.-
  N6: R1.Pin_0, U1.output_voltage
  N7: R1.Pin_1, U2.Pin_1
  N8: U1.input_voltage, Sensor_Pinouts.3, C1.+
  N9: U2.Pin_4, R2.Pin_1
  N10: U2.Pin_3, Output.1, Independent_Power_Supply_(24V).1
  N11: Sensor_Power_Supply_(24V).1, Sensor_Pinouts.1
